// Logisim project main.circ as structural Verilog: 1 circuit, main circuit main
module main (
);

  wire clock_1_out, clock_2_out, mem, not_1_out, read, word;
  wire [15:0] address_bus, cdm16_1_p6, cdm16_1_p7, data_bus;

  Clock clock_1 (.out(clock_1_out));
  // cdm16 cdm16_1: pin names not known; wires that end beside it: clock_1_out, mem, read, word, address_bus, cdm16_1_p6, cdm16_1_p7
  // Debugger debugger_1: pin names not known
  assign data_bus = not_1_out ? cdm16_1_p6 : 16'bz;  // Controlled_Buffer controlled_buffer_1
  not not_1 (not_1_out, read);
  assign cdm16_1_p7 = read ? data_bus : 16'bz;  // Controlled_Buffer controlled_buffer_2
  Clock clock_2 (.out(clock_2_out));
  // RAM ram_1: pin names not known; wires that end beside it: address_bus, word, mem, clock_2_out, read, data_bus
endmodule
